# Fritzing sketch Áramkör (saved by Fritzing 0.9.4)
breadboards: 1

parts:
  part = Raspberry Pi Zero
  part_2 = InvenSense MPU6050
  part_3 = InvenSense MPU6050
  part_4 = InvenSense MPU6050
  part_5 = InvenSense MPU6050
  part_6 = InvenSense MPU6050
  part_7 = InvenSense MPU6050
  part_8 = InvenSense MPU6050

nets:
  VCC: part.pin_1, part.pin_17, part_2.VCC, part_3.VCC, part_3.AD0, part_4.VCC, part_5.VCC, part_6.VCC, part_7.VCC, part_8.VCC
  N1: part.pin_3, part_2.SDA, part_3.SDA, part_4.SDA, part_5.SDA, part_6.SDA, part_7.SDA, part_8.SDA
  N2: part.pin_5, part_2.SCL, part_3.SCL, part_4.SCL, part_5.SCL, part_6.SCL, part_7.SCL, part_8.SCL
  GND: part.pin_6, part.pin_9, part.pin_14, part_2.GND, part_3.GND, part_4.GND, part_5.GND, part_6.GND, part_7.GND, part_8.GND
  N3: part.pin_13, part_2.AD0
  N4: part.pin_15, part_4.AD0
  N5: part.pin_31, part_5.AD0
  N6: part.pin_33, part_6.AD0
  N7: part.pin_35, part_7.AD0
  N8: part.pin_37, part_8.AD0
